# Fritzing sketch 4buttons (saved by Fritzing 0.9.2b)
breadboards: 1

parts:
  Part1 = Espruino Pico  # not connected
  S3 = Pushbutton [package="[SMD]"]
  S4 = Pushbutton [package="[SMD]"]
  S5 = Pushbutton [package="[SMD]"]
  S6 = Pushbutton [package="[SMD]"]

nets:
  N1: S3.Pin_1, S3.Pin_2
  N2: S3.Pin_3, S3.Pin_4, S4.Pin_3, S4.Pin_4, S5.Pin_3, S5.Pin_4, S6.Pin_1, S6.Pin_2
  N3: S4.Pin_1, S4.Pin_2
  N4: S5.Pin_1, S5.Pin_2
  N5: S6.Pin_3, S6.Pin_4

custom parts:
  Espruino Pico: Espruino is an Interactive JavaScript interpreter for Microcontrollers, so you can program them quickly and easily. The Espruino Pico is a specially designed board with Espruino software pre-installed. It complements the Espruino software with masses of functionality and great battery life.
